# Fritzing sketch lcd (saved by Fritzing 0.9.4)
breadboards: 1

parts:
  LCD1 = LCD screen
  Part1 = Arduino Uno (Rev3)
  R1 = Trimmer Potentiometer [maximum_resistance=10kΩ package=THT]

nets:
  VSS: LCD1.VSS, LCD1.V0, LCD1.RS, LCD1.R/W, LCD1.E, LCD1.DB0, LCD1.LED-, Part1.D11_PWM/MOSI, Part1.D12/MISO, Part1.GND
  VDD: LCD1.VDD, LCD1.LED+, Part1.5V, R1.leg2
  N1: LCD1.DB3, LCD1.DB4, LCD1.DB5, LCD1.DB6, LCD1.DB7, Part1.D2, Part1.D3_PWM, Part1.D4, Part1.D5_PWM
